# Fritzing sketch sailboatSchematics (saved by Fritzing 0.9.3b)
breadboards: 1

parts:
  Part1 = Arduino Mega 2560 (Rev3)
  U3 = EM408_CON [package=em408_con]
  Part2 = Compass Module - HMC6352
  FLO-30_Circuit1 = FLO-30 Circuit  # not connected
  Part3 = MicroSD Card Module  # not connected
  Part4 = 9 Degrees of Freedom - Sensor Stick
  U4 = LIPO-2000mAh [package=lipo-2000]
  BAT1 = Battery Holders [package=lipo-1100mAh]
  J1 = Basic Servo
  J2 = Basic Servo
  R4 = Resistor [tolerance=±5% resistance=10k package=THT]
  S2 = Momentary Switch [package=ksa_sealed_tac_switch]
  R5 = Resistor [tolerance=±5% resistance=10k package=THT]

nets:
  N1: Part1.D21/SCL, Part2.SCL
  N2: Part1.D20/SDA, Part2.SDA
  N3: Part1.D17_PWM/RX2, Part4.SDA
  N4: Part1.D16_PWM/TX2, Part4.SCL
  N5: Part1.D15/RX3, U3.RX
  N6: Part1.D9_PWM, J1.pulse
  N7: Part1.D8_PWM, J2.pulse
  3V3: Part1.3V3, Part2.VCC
  VCC: Part1.5V, U3.VCC, Part4.VCC, R4.Pin_0, S2.2, S2.4
  GND: Part1.GND, U3.GND, Part2.GND, Part4.GND, U4.-, BAT1.-, J1.gnd, J2.gnd, R5.Pin_0
  N8: Part1.VIN, U4.+
  N9: Part1.D2_PWM, S2.1, S2.3, R5.Pin_1
  VCC_2: BAT1.+, J1.vcc, J2.vcc

notes:
  9DOF will use UART serial ports. lets supose sda is tx and scl is rx (so we can use this part)
  COMPASS HMC6352
  GPS EM506
  Rudder Servo
  Sail Servo
  RED - 5v >
  ORANGE - 3.3v
  BLACK - gnd
  YELLOW - digital signal
  GREEN - analog signal
  BLUE - SDA
  PINK - SDL
  GREY - arduino's RX
  TEAL - arduino's TX
  Wind vane ground (blk) and signal (green) pins
  Anemometer
